# Fritzing sketch SandCastle (saved by Fritzing 0.9.1b)
breadboards: 1

parts:
  U1 = RF-LINK_RX [package=rf-link_rx]
  Part1 = Arduino Uno (Rev3) - ICSP

nets:
  GND: U1.GND, Part1.GND
  N1: U1.DATA, Part1.ICSP_MISO, Part1.D12/MISO
  +5V: U1.+5V, Part1.5V

notes:
  Antenna - 24cm wire
